// Logisim project lab4_1-g.circ as structural Verilog: 1 circuit, main circuit main
// 8
module main (
  input  A,
  input  B,
  input  C,
  input  D,
  output out_5,
  output out_6,
  output out_7,
  output out_8
);

  wire and_1_out, and_2_out, and_3_out, and_4_out, and_5_out, and_6_out, and_7_out, and_8_out, not_1_out,
       not_2_out, not_3_out, not_4_out;

  // Probe on {A, B, C, D}
  not not_1 (not_1_out, A);
  not not_2 (not_2_out, B);
  not not_3 (not_3_out, C);
  not not_4 (not_4_out, D);
  and and_1 (and_1_out, not_1_out, B, not_3_out, not_4_out);
  and and_2 (and_2_out, not_1_out, not_2_out, C, D);
  and and_3 (and_3_out, not_1_out, not_2_out, not_4_out);
  and and_4 (and_4_out, not_1_out, not_2_out, not_3_out);
  and and_5 (and_5_out, not_1_out, not_2_out, not_3_out, D);
  and and_6 (and_6_out, not_1_out, not_2_out, C, not_4_out);
  and and_7 (and_7_out, not_1_out, not_2_out, not_4_out);
  and and_8 (and_8_out, not_1_out, not_3_out, not_4_out);
  or or_1 (out_5, and_1_out, and_2_out);
  or or_2 (out_6, and_3_out, and_4_out);
  or or_3 (out_7, and_5_out, and_6_out);
  or or_4 (out_8, and_7_out, and_8_out);
  // Probe on {out_5, out_6, out_7, out_8}

  // Notes on the sheet:
  //   b
  //   a
  //   c
  //   d
  //   !a
  //   !c
  //   !b
  //   !d
endmodule
